# Fritzing sketch Untitled Sketch (saved by Fritzing 0.9.3b)
breadboards: 1

parts:
  LPC1114ETF1 = LPC1114ETF razvojni sistem
  Part1 = WiFi module 8266 [package=2x5-raf]
  Banggood_Display1 = Banggood Display

nets:
  N1: LPC1114ETF1.dp1, Banggood_Display1.SDO
  N2: LPC1114ETF1.dp2, Banggood_Display1.SDI
  N3: LPC1114ETF1.dp6, Banggood_Display1.SCK
  N4: LPC1114ETF1.dp15, Part1.1
  N5: LPC1114ETF1.dp16, Part1.8
  N6: LPC1114ETF1.dp23, Banggood_Display1.RST
  N7: LPC1114ETF1.dp24, Banggood_Display1.CS
  N8: LPC1114ETF1.dp25, Banggood_Display1.DC
  N9: LPC1114ETF1.GND#21, Part1.2
  N10: LPC1114ETF1.GND#22, Banggood_Display1.GND
  +3.3V: LPC1114ETF1.+3.3V, Banggood_Display1.VCC, Banggood_Display1.LED
  N11: Part1.3, Part1.5, Part1.7
